# Fritzing sketch single-line (saved by Fritzing 0.9.6b)
breadboards: 1

parts:
  D1 = Diode [package=diode-1n4001]
  D2 = Diode [package=diode-1n4001]
  U1 = MOC3031-M [package=dil06]
  U2 = MOC3031-M [package=dil06]
  J1 = Camdenboss CTB0158-3 [package=THT]
  J2 = Camdenboss CTB0158-2 [package=THT]
  R1 = Resistor [tolerance=±5% resistance=390 package="2010 [SMD]"]
  R2 = Resistor [tolerance=±5% resistance=390 package="2010 [SMD]"]
  F1 = Resettable Fuse PTC [package=0603]

nets:
  N1: D1.A, U2.6
  N2: D1.C, D2.A, J2.pin2
  N3: D2.C, U1.4
  N4: U1.1, R1.Pin_1
  N5: U1.2, U2.2, J1.pin2
  N6: U1.6, U2.4, F1.1
  N7: U2.1, R2.Pin_1
  N8: J1.pin1, R2.Pin_0
  N9: J1.pin3, R1.Pin_0
  N10: J2.pin1, F1.2
